// Logisim project alu.circ as structural Verilog: 1 circuit, main circuit alu
module alu (
  input  [31:0] A,
  input  [31:0] B,
  input  [3:0] ALUSel,
  output [31:0] Result
);

  wire comparator_1_lt, xor_1_out;
  wire [4:0] bit_extender_1_out, bit_extender_2_out, bit_extender_3_out;
  wire [31:0] add, and1, divu, mulh, mulhu, mult, multiplexer_1_out, multiplexer_2_out, multiplier_2_cout,
       negator_1_out, negator_2_out, not_1_out, or1, remu, sll1, slt1, sra1, srl1, sub, xor1;

  Bit_Extender #(.in_width(32), .out_width(5)) bit_extender_1 (.in(B), .out(bit_extender_1_out));
  Bit_Extender #(.in_width(32), .out_width(5)) bit_extender_2 (.in(B), .out(bit_extender_2_out));
  Bit_Extender #(.in_width(32), .out_width(5)) bit_extender_3 (.in(B), .out(bit_extender_3_out));
  Shifter #(.width(32), .shift("lr")) shifter_1 (.in(A), .\dist (bit_extender_1_out), .out(srl1));
  Shifter #(.width(32)) shifter_2 (.in(A), .\dist (bit_extender_2_out), .out(sll1));
  Shifter #(.width(32), .shift("ar")) shifter_3 (.in(A), .\dist (bit_extender_3_out), .out(sra1));
  Multiplexer #(.width(32), .enable("false")) multiplexer_1 (
    .in0(B), .in1(negator_2_out), .out(multiplexer_1_out), .sel(B[31]));
  Negator #(.width(32)) negator_1 (.in(A), .out(negator_1_out));
  Multiplexer #(.width(32), .enable("false")) multiplexer_2 (
    .in0(A), .in1(negator_1_out), .out(multiplexer_2_out), .sel(A[31]));
  Negator #(.width(32)) negator_2 (.in(B), .out(negator_2_out));
  xor xor_1 (xor_1_out, B[31], A[31]);
  Multiplexer #(.width(32), .enable("false")) multiplexer_3 (
    .in0(multiplier_2_cout), .in1(not_1_out), .out(mulh), .sel(xor_1_out));
  assign and1 = A & B;  // AND_Gate and_1, 32 bits wide
  Adder #(.width(32)) adder_1 (.a(A), .b(B), .out(add));  // open: cin, cout
  Comparator #(.width(32)) comparator_1 (.a(A), .b(B), .lt(comparator_1_lt));  // open: gt, eq
  Divider #(.width(32)) divider_1 (.a(A), .b(B), .out(divu), .rem(remu));  // open: upper
  Subtractor #(.width(32)) subtractor_1 (.a(A), .b(B), .out(sub));  // open: bin, bout
  Multiplier #(.width(32)) multiplier_1 (.a(A), .b(B), .out(mult), .cout(mulhu));  // open: cin
  Multiplier #(.width(32)) multiplier_2 (
    .a(multiplexer_2_out), .b(multiplexer_1_out), .cout(multiplier_2_cout));  // open: out, cin
  assign slt1 = {{31{1'b0}}, comparator_1_lt};  // Bit_Extender bit_extender_4
  not not_1 (not_1_out[0], multiplier_2_cout[0]);
  not not_2 (not_1_out[1], multiplier_2_cout[1]);
  not not_3 (not_1_out[3], multiplier_2_cout[3]);
  not not_4 (not_1_out[4], multiplier_2_cout[4]);
  not not_5 (not_1_out[5], multiplier_2_cout[5]);
  not not_6 (not_1_out[7], multiplier_2_cout[7]);
  not not_7 (not_1_out[8], multiplier_2_cout[8]);
  not not_8 (not_1_out[9], multiplier_2_cout[9]);
  not not_9 (not_1_out[11], multiplier_2_cout[11]);
  not not_10 (not_1_out[12], multiplier_2_cout[12]);
  not not_11 (not_1_out[13], multiplier_2_cout[13]);
  not not_12 (not_1_out[15], multiplier_2_cout[15]);
  not not_13 (not_1_out[16], multiplier_2_cout[16]);
  not not_14 (not_1_out[17], multiplier_2_cout[17]);
  not not_15 (not_1_out[19], multiplier_2_cout[19]);
  not not_16 (not_1_out[20], multiplier_2_cout[20]);
  not not_17 (not_1_out[21], multiplier_2_cout[21]);
  not not_18 (not_1_out[23], multiplier_2_cout[23]);
  not not_19 (not_1_out[24], multiplier_2_cout[24]);
  not not_20 (not_1_out[25], multiplier_2_cout[25]);
  not not_21 (not_1_out[27], multiplier_2_cout[27]);
  not not_22 (not_1_out[28], multiplier_2_cout[28]);
  not not_23 (not_1_out[29], multiplier_2_cout[29]);
  not not_24 (not_1_out[31], multiplier_2_cout[31]);
  not not_25 (not_1_out[2], multiplier_2_cout[2]);
  not not_26 (not_1_out[6], multiplier_2_cout[6]);
  not not_27 (not_1_out[10], multiplier_2_cout[10]);
  not not_28 (not_1_out[14], multiplier_2_cout[14]);
  not not_29 (not_1_out[18], multiplier_2_cout[18]);
  not not_30 (not_1_out[22], multiplier_2_cout[22]);
  not not_31 (not_1_out[26], multiplier_2_cout[26]);
  not not_32 (not_1_out[30], multiplier_2_cout[30]);
  assign or1 = A | B;  // OR_Gate or_1, 32 bits wide
  assign xor1 = A ^ B;  // XOR_Gate xor_2, 32 bits wide
  Multiplexer #(.select(4), .width(32), .enable("false")) multiplexer_4 (
    .in0(add), .in1(and1), .in2(or1), .in3(xor1), .in4(srl1), .in5(sra1), .in6(sll1), .in7(slt1), .in8(divu),
    .in9(remu), .in10(mult), .in11(mulhu), .in12(sub), .in13(B), .in14(mulh), .out(Result), .sel(ALUSel));  // open: in15

  // Other names for the same wires on the sheet: bsel[31:0] = B

  // Notes on the sheet:
  //   INPUTS to your circuit
  //   DON'T CHANGE THE LOCATIONS OF THE INPUTS AND OUTPUTS!
  //   OUTPUT from your circuit
endmodule
