// Logisim project cpu.circ as structural Verilog: 4 circuits, main circuit main
module main (
  input  [31:0] INSTRUCTION,
  input  CLOCK,
  output [31:0] FETCH_ADDRESS,
  output [31:0] ra,
  output [31:0] sp,
  output [31:0] t0,
  output [31:0] t1,
  output [31:0] t2,
  output [31:0] s0,
  output [31:0] s1,
  output [31:0] a0
);

  wire ASel, BrEq, BrLt, BrUn, BSel, MemRW, PCSel, RegWEn;
  wire [2:0] Address, funct3, ImmSel, WBSel;
  wire [3:0] ALUSel;
  wire [6:0] funct7, opcode;
  wire [7:0] DMEM_p5, DMEM_p5_2, DMEM_p5_3, DMEM_p5_4, multiplexer_6_out;
  wire [15:0] multiplexer_7_out;
  wire [17:0] imm;
  wire [31:0] adder_1_out, ALUPre, ALUResult, bit_extender_1_out, bit_extender_2_out, divider_1_out,
       divider_2_out, immProduced, multiplexer_1_out, multiplexer_2_out, multiplexer_3_out,
       multiplexer_4_out, multiplier_1_out, PC, PCPlus, ReadData1, ReadData2, Remainder, WBData;

  Adder #(.width(32)) adder_1 (.a(FETCH_ADDRESS), .b(32'h1), .out(adder_1_out));  // open: cin, cout
  Multiplexer #(.width(32), .enable("false")) multiplexer_1 (
    .in0(adder_1_out), .in1(divider_1_out), .out(multiplexer_1_out), .sel(PCSel));
  Divider #(.width(32)) divider_1 (.a(ALUResult), .b(32'h4), .out(divider_1_out));  // open: upper, rem
  Register #(.width(32)) u_PC (.D(multiplexer_1_out), .clk(CLOCK), .Q(FETCH_ADDRESS));  // open: en, clr
  Register #(.width(32)) PCPIPE (.D(multiplier_1_out), .clk(CLOCK), .Q(PC));  // open: en, clr
  Multiplier #(.width(32)) multiplier_1 (.a(FETCH_ADDRESS), .b(32'h4), .out(multiplier_1_out));  // open: cin, cout
  Register #(.width(32)) INSTR (
    .D(multiplexer_2_out), .clk(CLOCK), .Q({funct7, imm[17:8], funct3, imm[4:0], opcode}));  // open: en, clr
  Multiplexer #(.width(32), .enable("false")) multiplexer_2 (
    .in0(INSTRUCTION), .in1(32'h13), .out(multiplexer_2_out), .sel(PCSel));
  Adder #(.width(32)) adder_2 (.a(PC), .b(32'h4), .out(PCPlus));  // open: cin, cout
  ImmGen immgen_1 (.in_1({funct7, imm[17:8], funct3, imm[4:0]}), .in_2(ImmSel), .out_3(immProduced));
  ControlModule controlmodule_1 (
    .funct3(funct3), .funct7(funct7), .opcode(opcode), .BrEq(BrEq), .BrLt(BrLt), .ALUSel(ALUSel),
    .MemRW(MemRW), .PCSel(PCSel), .RegWEn(RegWEn), .ASel(ASel), .BSel(BSel), .BrUn(BrUn), .WBSel(WBSel),
    .ImmSel(ImmSel), .Address(Address));
  BranchComp branchcomp_1 (.ReadData1(ReadData1), .ReadData2(ReadData2), .BrUn(BrUn), .BrEq(BrEq), .BrLt(BrLt));
  regfile_main RegFile (
    .rs2(imm[17:13]), .rd(imm[4:0]), .Read_Data_1(ReadData1), .Read_Data_2(ReadData2), .ra(ra), .sp(sp),
    .t0(t0), .t1(t1), .t2(t2), .s0(s0), .s1(s1), .a0(a0), .rs1(imm[12:8]), .Write_Data(WBData),
    .RegWEn(RegWEn), .clk(CLOCK));  // open: zero
  Multiplexer #(.width(32), .enable("false")) multiplexer_3 (
    .in0(ReadData1), .in1(PC), .out(multiplexer_3_out), .sel(ASel));
  Multiplexer #(.width(32), .enable("false")) multiplexer_4 (
    .in0(ReadData2), .in1(immProduced), .out(multiplexer_4_out), .sel(BSel));
  Divider #(.width(32)) divider_2 (.a(ALUPre), .b(32'h4), .out(divider_2_out), .rem(Remainder));  // open: upper
  Multiplexer #(.select(3), .width(32), .enable("false")) multiplexer_5 (
    .in0(divider_2_out), .in1(divider_2_out), .in2(divider_2_out), .in3(divider_2_out), .in4(ALUPre),
    .out(ALUResult), .sel(Address));  // open: in5, in6, in7
  alu Arithmetic_Logic_Unit (.A(multiplexer_3_out), .B(multiplexer_4_out), .ALUSel(ALUSel), .Result(ALUPre));
  Multiplexer #(.select(2), .width(8), .enable("false")) multiplexer_6 (
    .in0(DMEM_p5), .in1(DMEM_p5_2), .in2(DMEM_p5_3), .in3(DMEM_p5_4), .out(multiplexer_6_out),
    .sel(Remainder[1:0]));
  Multiplexer #(.select(2), .width(16), .enable("false")) multiplexer_7 (
    .in0({DMEM_p5_2, DMEM_p5}), .in1({DMEM_p5_4, DMEM_p5_3}), .in2({DMEM_p5_2, DMEM_p5}),
    .in3({DMEM_p5_4, DMEM_p5_3}), .out(multiplexer_7_out), .sel(Remainder[1:0]));
  assign bit_extender_1_out = {{24{multiplexer_6_out[7]}}, multiplexer_6_out};  // Bit_Extender bit_extender_1
  assign bit_extender_2_out = {{16{multiplexer_7_out[15]}}, multiplexer_7_out};  // Bit_Extender bit_extender_2
  // mem_main DMEM: pin names not known; wires that end beside it: ALUResult, ReadData2, MemRW, CLOCK, {DMEM_p5_4, DMEM_p5_3, DMEM_p5_2, DMEM_p5}
  Multiplexer #(.select(3), .width(32), .enable("false")) multiplexer_8 (
    .in0(PCPlus), .in1(ALUResult), .in2({DMEM_p5_4, DMEM_p5_3, DMEM_p5_2, DMEM_p5}),
    .in3(bit_extender_1_out), .in4(bit_extender_2_out), .out(WBData), .sel(WBSel));  // open: in5, in6, in7

  // Other names for the same wires on the sheet: rd[4:0] = imm[4:0]; imm (some bits) = {funct7, funct3};
  //   rs1[4:0] = imm[12:8]; rs2[4:0] = imm[17:13]; clk = CLOCK; fetch_addr[31:0] = FETCH_ADDRESS

  // Notes on the sheet:
  //   Output
  //   Inputs/Outputs from run.circ. DO NOT MOVE THESE.
  //   Inputs
  //   Inputs/Outputs from run.circ. DO NOT MOVE THESE.
endmodule

module ImmGen (
  input  [24:0] in_1,
  input  [2:0] in_2,
  output [31:0] out_3
);

  wire [31:0] I, S, SB, UJ;

  assign I = {{20{in_1[24]}}, in_1[24:13]};  // Bit_Extender bit_extender_1
  assign S = {{20{in_1[24]}}, {in_1[24:18], in_1[4:0]}};  // Bit_Extender bit_extender_2
  assign SB = {{19{in_1[24]}}, {in_1[24], in_1[0], in_1[23:18], in_1[4:1], 1'b0}};  // Bit_Extender bit_extender_3
  assign UJ = {{11{in_1[24]}}, {in_1[24], in_1[12:5], in_1[13], in_1[23:14], 1'b0}};  // Bit_Extender bit_extender_4
  Multiplexer #(.select(3), .width(32), .enable("false")) multiplexer_1 (
    .in1(I), .in2(S), .in3(SB), .in4({in_1[24:5], {12{1'b0}}}), .in5(UJ), .out(out_3), .sel(in_2));  // open: in0, in6, in7

  // Other names for the same wires on the sheet: immS[11:0] = {in_1[24:18], in_1[4:0]};
  //   immSB[12:1] = {in_1[24], in_1[0], in_1[23:18], in_1[4:1]}; immI[11:0] = in_1[24:13]; immU[19:0] = in_1[24:5];
  //   immUJ[20:1] = {in_1[24], in_1[12:5], in_1[13], in_1[23:14]}; U[31:12] = in_1[24:5]
endmodule

module ControlModule (
  input  [2:0] funct3,
  input  [6:0] funct7,
  input  [6:0] opcode,
  input  BrEq,
  input  BrLt,
  output [3:0] ALUSel,
  output MemRW,
  output PCSel,
  output RegWEn,
  output ASel,
  output BSel,
  output BrUn,
  output [2:0] WBSel,
  output [2:0] ImmSel,
  output [2:0] Address
);

  wire and_1_out, and_2_out, and_3_out, and_4_out, and_5_out, and_6_out, and_7_out, and_8_out, and_9_out,
       and_10_out, and_11_out, and_12_out, and_13_out, and_14_out, and_15_out, and_16_out, and_17_out,
       and_18_out, and_19_out, and_20_out, and_21_out, and_22_out, and_23_out, and_24_out, and_25_out,
       and_26_out, and_27_out, and_28_out, and_29_out, and_30_out, and_31_out, and_32_out, and_33_out, F3eq0,
       F3eq1, F3eq2, F3eq3, F3eq4, F3eq5, F3eq6, F3eq7, F7eq0, F7eq1, F7eq20, not_1_out, OPeq03, OPeq6f,
       OPeq13, OPeq23, OPeq33, OPeq37, OPeq63, OPeq67, or_1_out, or_2_out, or_3_out, or_4_out, or_5_out,
       or_6_out, or_7_out, or_8_out, or_9_out, or_10_out, or_11_out, or_12_out, or_13_out, or_14_out;

  Comparator #(.width(3)) comparator_1 (.a(funct3), .b(3'b000), .eq(F3eq0));  // open: gt, lt
  Comparator #(.width(3)) comparator_2 (.a(funct3), .b(3'b001), .eq(F3eq1));  // open: gt, lt
  Comparator #(.width(3)) comparator_3 (.a(funct3), .b(3'b010), .eq(F3eq2));  // open: gt, lt
  Comparator #(.width(3)) comparator_4 (.a(funct3), .b(3'b011), .eq(F3eq3));  // open: gt, lt
  Comparator #(.width(3)) comparator_5 (.a(funct3), .b(3'b100), .eq(F3eq4));  // open: gt, lt
  Comparator #(.width(3)) comparator_6 (.a(funct3), .b(3'b101), .eq(F3eq5));  // open: gt, lt
  Comparator #(.width(3)) comparator_7 (.a(funct3), .b(3'b110), .eq(F3eq6));  // open: gt, lt
  Comparator #(.width(3)) comparator_8 (.a(funct3), .b(3'b111), .eq(F3eq7));  // open: gt, lt
  Comparator #(.width(7)) comparator_9 (.a(funct7), .b({7{1'b0}}), .eq(F7eq0));  // open: gt, lt
  Comparator #(.width(7)) comparator_10 (.a(funct7), .b(7'b0000001), .eq(F7eq1));  // open: gt, lt
  Comparator #(.width(7)) comparator_11 (.a(funct7), .b(7'b0100000), .eq(F7eq20));  // open: gt, lt
  Comparator #(.width(7)) comparator_12 (.a(opcode), .b(7'b0000011), .eq(OPeq03));  // open: gt, lt
  Comparator #(.width(7)) comparator_13 (.a(opcode), .b(7'b0010011), .eq(OPeq13));  // open: gt, lt
  Comparator #(.width(7)) comparator_14 (.a(opcode), .b(7'b0100011), .eq(OPeq23));  // open: gt, lt
  Comparator #(.width(7)) comparator_15 (.a(opcode), .b(7'b0110011), .eq(OPeq33));  // open: gt, lt
  Comparator #(.width(7)) comparator_16 (.a(opcode), .b(7'b1100011), .eq(OPeq63));  // open: gt, lt
  Comparator #(.width(7)) comparator_17 (.a(opcode), .b(7'b0110111), .eq(OPeq37));  // open: gt, lt
  Comparator #(.width(7)) comparator_18 (.a(opcode), .b(7'b1101111), .eq(OPeq6f));  // open: gt, lt
  Comparator #(.width(7)) comparator_19 (.a(opcode), .b(7'b1100111), .eq(OPeq67));  // open: gt, lt
  or or_1 (or_1_out, and_25_out, and_24_out, and_27_out, and_26_out);
  and and_1 (and_1_out, F3eq2, OPeq03);
  Multiplexer #(.enable("false")) multiplexer_1 (.in0(1'b0), .in1(1'b1), .out(MemRW), .sel(OPeq23));
  not not_1 (not_1_out, BrEq);
  and and_2 (and_2_out, F3eq0, OPeq03);
  and and_3 (and_3_out, F3eq1, OPeq03);
  and and_4 (and_4_out, F3eq0, F7eq0, OPeq33);
  and and_5 (and_5_out, F3eq7, F7eq0, OPeq33);
  and and_6 (and_6_out, F3eq6, F7eq0, OPeq33);
  and and_7 (and_7_out, F3eq4, F7eq0, OPeq33);
  and and_8 (and_8_out, F3eq5, F7eq0, OPeq33);
  and and_9 (and_9_out, F3eq5, F7eq20, OPeq13);
  and and_10 (and_10_out, F3eq1, F7eq0, OPeq33);
  and and_11 (and_11_out, F3eq1, F7eq0, OPeq13);
  and and_12 (and_12_out, F3eq2, F7eq0, OPeq33);
  and and_13 (and_13_out, F3eq5, OPeq33, F7eq1);
  and and_14 (and_14_out, F3eq7, OPeq33, F7eq1);
  and and_15 (and_15_out, F3eq0, OPeq33, F7eq1);
  and and_16 (and_16_out, F3eq3, OPeq33, F7eq1);
  and and_17 (and_17_out, F3eq0, OPeq33, F7eq20);
  and and_18 (and_18_out, F3eq1, OPeq33, F7eq1);
  and and_19 (and_19_out, BrEq, F3eq0, OPeq63);
  and and_20 (and_20_out, not_1_out, F3eq1, OPeq63);
  and and_21 (and_21_out, BrLt, F3eq4, OPeq63);
  and and_22 (and_22_out, BrLt, F3eq6, OPeq63);
  or or_2 (or_2_out, OPeq23, OPeq63);
  or or_3 (or_3_out, OPeq63, OPeq37, OPeq6f);
  and and_23 (and_23_out, OPeq63, F3eq6);
  or or_4 (or_4_out, OPeq13, OPeq33, OPeq37);
  or or_5 (or_5_out, OPeq6f, OPeq67);
  or or_6 (or_6_out, OPeq03, OPeq67, OPeq13);
  and and_24 (and_24_out, F3eq0, OPeq03);
  and and_25 (and_25_out, F3eq1, OPeq03);
  and and_26 (and_26_out, F3eq2, OPeq03);
  and and_27 (and_27_out, F3eq2, OPeq23);
  and and_28 (and_28_out, F3eq0, OPeq13);
  or or_7 (or_7_out, and_5_out, and_29_out);
  and and_29 (and_29_out, F3eq7, OPeq13);
  or or_8 (or_8_out, and_6_out, and_30_out);
  and and_30 (and_30_out, F3eq6, OPeq13);
  or or_9 (or_9_out, and_7_out, and_31_out);
  and and_31 (and_31_out, F3eq4, OPeq13);
  or or_10 (or_10_out, and_8_out, and_32_out);
  and and_32 (and_32_out, F3eq5, OPeq13);
  or or_11 (or_11_out, and_10_out, and_11_out);
  or or_12 (or_12_out, and_12_out, and_33_out);
  and and_33 (and_33_out, F3eq2, OPeq13);
  Multiplexer #(.enable("false")) multiplexer_2 (.in0(1'b1), .in1(1'b0), .out(RegWEn), .sel(or_2_out));
  Multiplexer #(.enable("false")) multiplexer_3 (.in0(1'b0), .in1(1'b1), .out(ASel), .sel(or_3_out));
  Multiplexer #(.enable("false")) multiplexer_4 (.in0(1'b1), .in1(1'b0), .out(BSel), .sel(OPeq33));
  Multiplexer #(.enable("false")) multiplexer_5 (.in0(1'b0), .in1(1'b1), .out(BrUn), .sel(and_23_out));
  Multiplexer #(.width(3), .enable("false")) multiplexer_6 (.in1(3'b001), .out(WBSel), .sel(or_4_out));  // open: in0
  Multiplexer #(.width(3), .enable("false")) multiplexer_7 (.in1(3'b010), .out(WBSel), .sel(and_1_out));  // open: in0
  Multiplexer #(.width(3), .enable("false")) multiplexer_8 (.in1(3'b000), .out(WBSel), .sel(or_5_out));  // open: in0
  Multiplexer #(.width(3), .enable("false")) multiplexer_9 (.in1(3'b011), .out(WBSel), .sel(and_2_out));  // open: in0
  Multiplexer #(.width(3), .enable("false")) multiplexer_10 (.in1(3'b100), .out(WBSel), .sel(and_3_out));  // open: in0
  Multiplexer #(.width(3), .enable("false")) multiplexer_11 (.in1(3'b001), .out(ImmSel), .sel(or_6_out));  // open: in0
  Multiplexer #(.width(3), .enable("false")) multiplexer_12 (.in1(3'b010), .out(ImmSel), .sel(OPeq23));  // open: in0
  Multiplexer #(.width(3), .enable("false")) multiplexer_13 (.in1(3'b011), .out(ImmSel), .sel(OPeq63));  // open: in0
  Multiplexer #(.width(3), .enable("false")) multiplexer_14 (.in1(3'b100), .out(ImmSel), .sel(OPeq37));  // open: in0
  Multiplexer #(.width(3), .enable("false")) multiplexer_15 (.in1(3'b101), .out(ImmSel), .sel(OPeq6f));  // open: in0
  or or_13 (or_13_out, and_28_out, OPeq03, and_4_out, OPeq23, OPeq63, OPeq6f, OPeq67);
  Multiplexer #(.width(4), .enable("false")) multiplexer_16 (.in1(4'b0001), .out(ALUSel), .sel(or_7_out));  // open: in0
  Multiplexer #(.width(4), .enable("false")) multiplexer_17 (.in1(4'b0010), .out(ALUSel), .sel(or_8_out));  // open: in0
  Multiplexer #(.width(4), .enable("false")) multiplexer_18 (.in1(4'b0011), .out(ALUSel), .sel(or_9_out));  // open: in0
  Multiplexer #(.width(4), .enable("false")) multiplexer_19 (
    .in1(4'b0100), .out(ALUSel), .sel(or_10_out));  // open: in0
  Multiplexer #(.width(4), .enable("false")) multiplexer_20 (
    .in1(4'b0101), .out(ALUSel), .sel(and_9_out));  // open: in0
  Multiplexer #(.width(4), .enable("false")) multiplexer_21 (
    .in1(4'b0110), .out(ALUSel), .sel(or_11_out));  // open: in0
  Multiplexer #(.width(4), .enable("false")) multiplexer_22 (
    .in1(4'b0111), .out(ALUSel), .sel(or_12_out));  // open: in0
  Multiplexer #(.width(4), .enable("false")) multiplexer_23 (
    .in1(4'b1000), .out(ALUSel), .sel(and_13_out));  // open: in0
  Multiplexer #(.width(4), .enable("false")) multiplexer_24 (
    .in1(4'b1001), .out(ALUSel), .sel(and_14_out));  // open: in0
  Multiplexer #(.width(4), .enable("false")) multiplexer_25 (
    .in1(4'b1010), .out(ALUSel), .sel(and_15_out));  // open: in0
  Multiplexer #(.width(4), .enable("false")) multiplexer_26 (
    .in1(4'b1011), .out(ALUSel), .sel(and_16_out));  // open: in0
  Multiplexer #(.width(4), .enable("false")) multiplexer_27 (
    .in1(4'b1100), .out(ALUSel), .sel(and_17_out));  // open: in0
  Multiplexer #(.width(4), .enable("false")) multiplexer_28 (.in1(4'b1101), .out(ALUSel), .sel(OPeq37));  // open: in0
  Multiplexer #(.width(4), .enable("false")) multiplexer_29 (
    .in1(4'b1110), .out(ALUSel), .sel(and_18_out));  // open: in0
  Multiplexer #(.width(3), .enable("false")) multiplexer_30 (
    .in1(3'b000), .out(Address), .sel(and_24_out));  // open: in0
  Multiplexer #(.width(3), .enable("false")) multiplexer_31 (
    .in1(3'b001), .out(Address), .sel(and_25_out));  // open: in0
  Multiplexer #(.width(3), .enable("false")) multiplexer_32 (
    .in1(3'b010), .out(Address), .sel(and_26_out));  // open: in0
  Multiplexer #(.width(3), .enable("false")) multiplexer_33 (
    .in1(3'b011), .out(Address), .sel(and_27_out));  // open: in0
  Multiplexer #(.width(3), .enable("false")) multiplexer_34 (.in0(3'b100), .out(Address), .sel(or_1_out));  // open: in1
  Multiplexer #(.width(4), .enable("false")) multiplexer_35 (
    .in1(4'b0000), .out(ALUSel), .sel(or_13_out));  // open: in0
  Multiplexer #(.enable("false")) multiplexer_36 (.in0(1'b0), .in1(1'b1), .out(PCSel), .sel(or_14_out));
  or or_14 (or_14_out, OPeq6f, OPeq67, and_19_out, and_20_out, and_21_out, and_22_out);
endmodule

module BranchComp (
  input  [31:0] ReadData1,
  input  [31:0] ReadData2,
  input  BrUn,
  output BrEq,
  output BrLt
);

  wire comparator_1_eq, comparator_1_lt, comparator_2_eq, comparator_2_lt;

  Comparator #(.width(32)) comparator_1 (
    .a(ReadData1), .b(ReadData2), .eq(comparator_1_eq), .lt(comparator_1_lt));  // open: gt
  Comparator #(.width(32), .mode("unsigned")) comparator_2 (
    .a(ReadData1), .b(ReadData2), .eq(comparator_2_eq), .lt(comparator_2_lt));  // open: gt
  Multiplexer #(.enable("false")) multiplexer_1 (.in0(comparator_1_eq), .in1(comparator_2_eq), .out(BrEq), .sel(BrUn));
  Multiplexer #(.enable("false")) multiplexer_2 (.in0(comparator_1_lt), .in1(comparator_2_lt), .out(BrLt), .sel(BrUn));
endmodule
